# Fritzing sketch Phuc (saved by Fritzing 0.9.3b)
circuit board: 3.83049cm x 4.68526cm

parts:
  Part2 = Arduino Uno (Rev3) - ICSP
  X1 = X113647 Stepper Driver Board [package=board]
  U2 = MMA_ACCEL_CONNECTOR [package=1x08]

nets:
  N1: Part2.5V, U2.X
  N2: Part2.D8, X1.IN4
  N3: Part2.D9_PWM, X1.IN2
  N4: Part2.D10_PWM/SS, X1.IN3
  N5: Part2.D11_PWM/MOSI, X1.IN1
  GND: Part2.GND, U2.GND

notes:
  phuc

custom parts:
  X113647 Stepper Driver Board: A common stepper motor driver board based on ULN2003APG darlington array
