# Fritzing sketch PhucFritzing (saved by Fritzing 0.9.3b)
circuit board: 2.46741cm x 2.69958cm

parts:
  Part1 = Arduino Uno (Rev3)
  X1 = X113647 Stepper Driver Board [package=board]

nets:
  N1: Part1.D8, X1.IN4
  N2: Part1.D9_PWM, X1.IN2
  N3: Part1.D10_PWM/SS, X1.IN3
  N4: Part1.D11_PWM/MOSI, X1.IN1

notes:
  phuc

custom parts:
  X113647 Stepper Driver Board: A common stepper motor driver board based on ULN2003APG darlington array
